# Fritzing sketch schematic (saved by Fritzing 0.9.3b)
circuit board: 8.46667cm x 5.64444cm

parts:
  Part1 = Arduino Uno (Rev3)
  Part2 = Breakout Board for Electret Microphone
  Part3 = Matrix LED de 8x8 basada en MAX7219

nets:
  N1: Part1.A0, Part2.AUD
  N2: Part1.D9_PWM, Part3.CS
  N3: Part1.D11_PWM/MOSI, Part3.DIN
  N4: Part1.D13/SCK, Part3.CLK
  GND: Part1.GND, Part2.GND, Part3.GND
  3V3: Part1.AREF, Part1.3V3, Part2.VCC
  5V: Part1.5V, Part3.VCC
